// Logisim project KeyPad.circ as structural Verilog: 1 circuit, main circuit main
module main (
  input  s1,
  input  s0
);

  wire a3_out, a5_out, a8_out, button_1_out, button_2_out, button_4_out, button_6_out, button_7_out,
       button_9_out, gate0_out, gate3_out, xnor_1_out, xnor_2_out;
  wire [3:0] multiplexer_1_out, priority_encoder_1_out, undriven;

  Button a0 ();  // open: out
  Button button_1 (.out(button_1_out));
  Button a1 (.out(button_1_out));
  Button button_2 (.out(button_2_out));
  Button a2 (.out(button_2_out));
  Button a3 (.out(a3_out));
  Button button_3 (.out(a3_out));
  Button button_4 (.out(button_4_out));
  Button a4 (.out(button_4_out));
  Button a5 (.out(a5_out));
  Button button_5 (.out(a5_out));
  Button button_6 (.out(button_6_out));
  Button a6 (.out(button_6_out));
  Button button_7 (.out(button_7_out));
  Button a7 (.out(button_7_out));
  Button a8 (.out(a8_out));
  Button button_8 (.out(a8_out));
  Button button_9 (.out(button_9_out));
  Button a9 (.out(button_9_out));
  Priority_Encoder #(.select(4)) priority_encoder_1 (
    .in1(button_1_out), .in2(button_2_out), .in3(a3_out), .in4(button_4_out), .in5(a5_out),
    .in6(button_6_out), .in7(button_7_out), .in8(a8_out), .in9(button_9_out), .out(priority_encoder_1_out));  // open: in0, in10, in11, in12, in13, in14, in15, gs, en_out, en_in
  Decoder #(.select(2)) decoder_1 (.sel({s0, s1}), .en(1'b1));  // open: out0, out1, out2, out3
  Multiplexer #(.select(2), .width(4)) multiplexer_1 (
    .in0(4'b0101), .in1(4'b0011), .in2(4'b1001), .in3(4'b0001), .out(multiplexer_1_out), .sel({s0, s1}));
  xnor gate0 (gate0_out, undriven[0], multiplexer_1_out[0]);
  xnor xnor_1 (xnor_1_out, undriven[1], multiplexer_1_out[1]);
  xnor gate1 (xnor_1_out, undriven[1], multiplexer_1_out[1]);
  xnor xnor_2 (xnor_2_out, undriven[2], multiplexer_1_out[2]);
  xnor gate2 (xnor_2_out, undriven[2], multiplexer_1_out[2]);
  xnor gate3 (gate3_out, undriven[3], multiplexer_1_out[3]);
  // AND_Gate and_1 has open pins: in0=gate0_out, in1=xnor_1_out, in2=xnor_2_out, in3=gate3_out, out=open
endmodule
